# Fritzing sketch read-switches (saved by Fritzing 0.9.3b)
circuit board: 8.46667cm x 5.64444cm
breadboards: 1

parts:
  Q1 = NPN-Transistor [package="TO92 [THT]"]
  R2 = Resistor [tolerance=±5% resistance=10k package=THT]
  LED1 = LED - 5mm [color="Green (565nm)" package="5 mm [THT]"]
  R3 = Resistor [tolerance=±5% resistance=560 package=THT]
  Q2 = NPN-Transistor [package="TO92 [THT]"]
  R4 = Resistor [tolerance=±5% resistance=10k package=THT]
  LED2 = LED - 5mm [color="Yellow (592nm)" package="5 mm [THT]"]
  R5 = Resistor [tolerance=±5% resistance=560 package=THT]
  S1 = Reed switch [package=THT]
  Q3 = NPN-Transistor [package="TO92 [THT]"]
  R6 = Resistor [tolerance=±5% resistance=560 package=THT]
  R7 = Resistor [tolerance=±10% resistance=10k package=THT]
  Q4 = NPN-Transistor [package="TO92 [THT]"]
  R8 = Resistor [tolerance=±10% resistance=10k package=THT]
  R9 = Resistor [tolerance=±5% resistance=560 package=THT]
  Q5 = NPN-Transistor [package="TO92 [THT]"]
  R10 = Resistor [tolerance=±10% resistance=10k package=THT]
  R11 = Resistor [tolerance=±5% resistance=560 package=THT]
  S3 = Reed switch [package=THT]
  S4 = Momentary Switch [package=tactile-pth]
  R12 = Resistor [tolerance=±10% resistance=10k package=THT]
  Raspberry_Pi_1 = Raspberry Pi 3 [part_number=RPI-3-V1.2]
  S5 = Reed switch [package=THT]
  R13 = Resistor [tolerance=±10% resistance=1k package=THT]

nets:
  N1: Q1.E, LED1.anode
  N2: Q1.B, R2.Pin_0
  N3: Q1.C, Q2.C, R4.Pin_1, R7.Pin_0, R8.Pin_0, R10.Pin_0, R12.Pin_0, Raspberry_Pi_1.GND
  N4: R2.Pin_1, Raspberry_Pi_1.GPIO16
  N5: LED1.cathode, R3.Pin_1
  3V3: R3.Pin_0, R5.Pin_0, S1.pin_2, Q3.E, Q3.C, R7.Pin_1, Q4.E, Q5.E, S3.pin_2, S4.2, Raspberry_Pi_1.3v3, Raspberry_Pi_1.3V3, S5.pin_2
  N6: Q2.E, LED2.anode
  N7: Q2.B, R4.Pin_0
  N8: LED2.cathode, R5.Pin_1
  N9: S1.pin_1, R6.Pin_0
  N10: Q3.B, R6.Pin_1
  N11: Q4.B, R9.Pin_1
  N12: Q4.C, R8.Pin_1, Raspberry_Pi_1.GPIO23
  N13: R9.Pin_0, S5.pin_1
  N14: Q5.B, R11.Pin_1
  N15: Q5.C, R10.Pin_1, Raspberry_Pi_1.GPIO24
  N16: R11.Pin_0, S3.pin_1
  N17: S4.1, R12.Pin_1, R13.Pin_1
  N18: Raspberry_Pi_1.GPIO17, R13.Pin_0
